# Fritzing sketch Mimic_Project (saved by Fritzing 0.9.3b)
breadboards: 1

parts:
  Part1 = Tri-Axis Gyro Breakout - L3G4200D
  R1 = Basic Flex Resistor
  J1 = Basic Servo
  J2 = Basic Servo
  J3 = Basic Servo
  J4 = Basic Servo
  J5 = Basic Servo
  Part2 = Arduino Ethernet Shield (Rev3)
  LED1 = RGB LED (com. cathode, rbg) [package="5 mm [THT]"]  # not connected
  J6 = Piezo Speaker
  R2 = Resistor [tolerance=±5% resistance=220 package="0402 [SMD]"]

nets:
  GND: Part1.GND, R1.pin_1, J1.gnd, J2.gnd, J3.gnd, J4.gnd, J5.gnd, Part2.GND, J6.pin1
  VCC: Part1.VCC, Part2.3V3
  N1: Part1.SCL, Part2.A5/SCL
  N2: Part1.SDA, Part2.A4/SDA
  N3: R1.Pin_2, Part2.A0, R2.Pin_1
  VCC_2: J1.vcc, J2.vcc, J4.vcc, J5.vcc, Part2.5V, R2.Pin_0
